# Fritzing sketch giveMeTheBinary (saved by Fritzing 0.9.3b)
breadboards: 1

parts:
  Componente1 = Arduino Uno (Rev3)
  LED1 = LED - 5mm [color="Red (633nm)" package="5 mm [THT]"]
  LED2 = LED - 5mm [color="Green (555nm)" package="5 mm [THT]"]
  LED3 = LED - 5mm [color="Green (555nm)" package="5 mm [THT]"]
  LED4 = LED - 5mm [color="Green (555nm)" package="5 mm [THT]"]
  LED5 = LED - 5mm [color="Green (555nm)" package="5 mm [THT]"]
  S3 = Momentary Switch [package=ksa_sealed_tac_switch]
  R1 = Resistor [tolerance=±5% resistance=220 package=THT]
  R2 = Resistor [tolerance=±5% resistance=10k package=THT]
  S4 = Momentary Switch [package=ksa_sealed_tac_switch]
  R3 = Resistor [tolerance=±5% resistance=220 package=THT]
  R4 = Resistor [tolerance=±5% resistance=10k package=THT]
  S5 = Momentary Switch [package=ksa_sealed_tac_switch]
  R5 = Resistor [tolerance=±5% resistance=220 package=THT]
  R6 = Resistor [tolerance=±5% resistance=10k package=THT]
  S6 = Momentary Switch [package=ksa_sealed_tac_switch]
  R7 = Resistor [tolerance=±5% resistance=220 package=THT]
  R8 = Resistor [tolerance=±5% resistance=10k package=THT]
  R9 = Resistor [tolerance=±5% resistance=220 package=THT]
  R10 = Rotary Potentiometer (Small) [maximum_resistance=100kΩ package=THT]
  Display1 = LCD screen 16x2 IIC [part_number=101290]

nets:
  N1: Componente1.A0, R10.wiper
  N2: Componente1.A4/SDA, Display1.SDA
  N3: Componente1.A5/SCL, Display1.SCL
  N4: Componente1.D10_PWM/SS, R7.Pin_1
  N5: Componente1.D11_PWM/MOSI, R5.Pin_1
  N6: Componente1.D12/MISO, R3.Pin_1
  N7: Componente1.D13/SCK, R1.Pin_1
  N8: Componente1.D2, S3.4, R2.Pin_1
  N9: Componente1.D3_PWM, S4.4, R4.Pin_1
  N10: Componente1.D4, S5.4, R6.Pin_1
  N11: Componente1.D5_PWM, S6.4, R8.Pin_1
  N12: Componente1.D6_PWM, R9.Pin_1
  5V: Componente1.5V, S3.2, S4.2, S5.2, S6.2, Display1.VCC
  GND: Componente1.GND, LED1.cathode, LED2.cathode, LED3.cathode, LED4.cathode, LED5.cathode, R2.Pin_0, R4.Pin_0, R6.Pin_0, R8.Pin_0, R10.leg1, R10.leg2, Display1.GND
  N13: LED1.anode, R9.Pin_0
  N14: LED2.anode, R1.Pin_0
  N15: LED3.anode, R7.Pin_0
  N16: LED4.anode, R5.Pin_0
  N17: LED5.anode, R3.Pin_0

custom parts:
  LCD screen 16x2 IIC: LCD screen with HD44780 controller enables showing text, symbols, value or anything else that comes from Croduino/Arduino. It is capable of showing 16 symbols in two lines and therefore can be used in many projects that need to send clearly visible and legible output information.. • Color of symbols: White • Backlight: Blue • Dimensions: 80 x 36 x 12 mm • Screen dimensions: 64.5 x 16 mm •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
